# Fritzing sketch analog_board (saved by Fritzing 0.9.0b)
breadboards: 1

parts:
  IC1 = CD22M3494 [package=THT]  # not connected
  IC2 = CD22M3494 [package=THT]  # not connected
  Part1 = AD8403 [package=TSSOP]
  Part2 = AD8403 [package=TSSOP]
  Part3 = AD8403 [package=TSSOP]  # not connected
  Part4 = AD8403 [package=TSSOP]  # not connected
  JP1 = Header 8 [package=1x08_smd]  # not connected
  JP2 = Header 8 [package=1x08_smd]  # not connected
  IN_BOTTOM_1 = Header 8 [package=1x08_smd]
  IN_BOTTOM_2 = Header 8 [package=1x08_smd]  # not connected

nets:
  N1: Part1.3, IN_BOTTOM_1.2
  N2: Part1.7, IN_BOTTOM_1.4
  N3: Part1.19, IN_BOTTOM_1.3
  N4: Part1.23, IN_BOTTOM_1.1
  N5: Part2.3, IN_BOTTOM_1.6
  N6: Part2.7, IN_BOTTOM_1.8
  N7: Part2.19, IN_BOTTOM_1.7
  N8: Part2.23, IN_BOTTOM_1.5

custom parts:
  CD22M3494: CD22M3494 from Intersil http://www.icbase.com/pdf/ITS/ITS14170701.pdf
  AD8403: http://www.analog.com/static/imported-files/data_sheets/AD8400_8402_8403.pdf
