# Fritzing sketch arduino_shield (saved by Fritzing 0.9.0b)
breadboards: 1

parts:
  PDU = female pin header, 8 pins [form="♀ (female)"]
  J2 = female pin header, 8 pins [form="♀ (female)"]  # not connected
  J3 = female pin header, 8 pins [form="♀ (female)"]  # not connected
  J4 = female pin header, 8 pins [form="♀ (female)"]  # not connected
  I2C_JUMPERS = female pin header, 8 pins [form="♀ (female)"]
  J7 = female pin header, 10 pins [form="♀ (female)"]
  SWITCH_CTRL = double row female pin header, 16 pins [form="♀ (female)"]
  POT_CTRL = double row female pin header, 16 pins [form="♀ (female)"]
  SPI_JUMPERS = double row female pin header, 36 pins [form="♀ (female)"]
  BOTTOM_SHIFT_REGISTER = MCP23017 I2C I/O Expander
  TOP_SHIFT_REGISTER = MCP23017 I2C I/O Expander
  LEDS_TOP = double row female pin header, 16 pins [form="♀ (female)"]
  LEDS_BOTTOM = double row female pin header, 16 pins [form="♀ (female)"]
  R1 = Resistor [tolerance=±5% resistance=10k package=THT]
  R2 = Resistor [tolerance=±5% resistance=10k package=THT]

nets:
  GND: PDU.pin2, PDU.pin3, J7.pin7, SWITCH_CTRL.pin10, POT_CTRL.pin10, SPI_JUMPERS.pin1, SPI_JUMPERS.pin36, BOTTOM_SHIFT_REGISTER.VSS, BOTTOM_SHIFT_REGISTER.A1, BOTTOM_SHIFT_REGISTER.A2, TOP_SHIFT_REGISTER.VSS, TOP_SHIFT_REGISTER.A0, TOP_SHIFT_REGISTER.A1, TOP_SHIFT_REGISTER.A2
  5V: PDU.pin4, SWITCH_CTRL.pin9, POT_CTRL.pin9, SPI_JUMPERS.pin18, SPI_JUMPERS.pin19, BOTTOM_SHIFT_REGISTER.VDD, BOTTOM_SHIFT_REGISTER.A0, TOP_SHIFT_REGISTER.VDD, R1.Pin_1, R2.Pin_1
  N1: I2C_JUMPERS.pin1, BOTTOM_SHIFT_REGISTER.SCL, TOP_SHIFT_REGISTER.SCL
  N2: I2C_JUMPERS.pin2, BOTTOM_SHIFT_REGISTER.SDA, TOP_SHIFT_REGISTER.SDA
  N3: SWITCH_CTRL.pin1, SPI_JUMPERS.pin29
  N4: SWITCH_CTRL.pin2, SPI_JUMPERS.pin28
  N5: SWITCH_CTRL.pin3, SPI_JUMPERS.pin27
  N6: SWITCH_CTRL.pin4, SPI_JUMPERS.pin26
  N7: SWITCH_CTRL.pin5, SPI_JUMPERS.pin25
  N8: SWITCH_CTRL.pin6, SPI_JUMPERS.pin24
  N9: SWITCH_CTRL.pin7, SPI_JUMPERS.pin23
  N10: SWITCH_CTRL.pin8, SPI_JUMPERS.pin22
  N11: SWITCH_CTRL.pin11, SPI_JUMPERS.pin13
  N12: SWITCH_CTRL.pin12, SPI_JUMPERS.pin12
  N13: SWITCH_CTRL.pin13, SPI_JUMPERS.pin11
  N14: SWITCH_CTRL.pin14, SPI_JUMPERS.pin10
  N15: SWITCH_CTRL.pin15, SPI_JUMPERS.pin9
  N16: SWITCH_CTRL.pin16, SPI_JUMPERS.pin8
  N17: POT_CTRL.pin1, SPI_JUMPERS.pin3
  N18: POT_CTRL.pin2, SPI_JUMPERS.pin5
  N19: POT_CTRL.pin3, SPI_JUMPERS.pin32
  N20: POT_CTRL.pin4, SPI_JUMPERS.pin7
  N21: POT_CTRL.pin5, SPI_JUMPERS.pin30
  N22: POT_CTRL.pin12, SPI_JUMPERS.pin31
  N23: POT_CTRL.pin13, SPI_JUMPERS.pin6
  N24: POT_CTRL.pin14, SPI_JUMPERS.pin33
  N25: POT_CTRL.pin15, SPI_JUMPERS.pin4
  N26: POT_CTRL.pin16, SPI_JUMPERS.pin35
  N27: BOTTOM_SHIFT_REGISTER.GPB0, LEDS_BOTTOM.pin9
  N28: BOTTOM_SHIFT_REGISTER.GPB1, LEDS_BOTTOM.pin10
  N29: BOTTOM_SHIFT_REGISTER.GPB2, LEDS_BOTTOM.pin11
  N30: BOTTOM_SHIFT_REGISTER.GPB3, LEDS_BOTTOM.pin12
  N31: BOTTOM_SHIFT_REGISTER.GPB4, LEDS_BOTTOM.pin13
  N32: BOTTOM_SHIFT_REGISTER.GPB5, LEDS_BOTTOM.pin14
  N33: BOTTOM_SHIFT_REGISTER.GPB6, LEDS_BOTTOM.pin15
  N34: BOTTOM_SHIFT_REGISTER.GPB7, LEDS_BOTTOM.pin16
  N35: BOTTOM_SHIFT_REGISTER.RESET, R2.Pin_0
  N36: BOTTOM_SHIFT_REGISTER.GPA0, LEDS_BOTTOM.pin1
  N37: BOTTOM_SHIFT_REGISTER.GPA1, LEDS_BOTTOM.pin2
  N38: BOTTOM_SHIFT_REGISTER.GPA2, LEDS_BOTTOM.pin3
  N39: BOTTOM_SHIFT_REGISTER.GPA3, LEDS_BOTTOM.pin4
  N40: BOTTOM_SHIFT_REGISTER.GPA4, LEDS_BOTTOM.pin5
  N41: BOTTOM_SHIFT_REGISTER.GPA5, LEDS_BOTTOM.pin6
  N42: BOTTOM_SHIFT_REGISTER.GPA6, LEDS_BOTTOM.pin7
  N43: BOTTOM_SHIFT_REGISTER.GPA7, LEDS_BOTTOM.pin8
  N44: TOP_SHIFT_REGISTER.GPB0, LEDS_TOP.pin9
  N45: TOP_SHIFT_REGISTER.GPB1, LEDS_TOP.pin10
  N46: TOP_SHIFT_REGISTER.GPB2, LEDS_TOP.pin11
  N47: TOP_SHIFT_REGISTER.GPB3, LEDS_TOP.pin12
  N48: TOP_SHIFT_REGISTER.GPB4, LEDS_TOP.pin13
  N49: TOP_SHIFT_REGISTER.GPB5, LEDS_TOP.pin14
  N50: TOP_SHIFT_REGISTER.GPB6, LEDS_TOP.pin15
  N51: TOP_SHIFT_REGISTER.GPB7, LEDS_TOP.pin16
  N52: TOP_SHIFT_REGISTER.RESET, R1.Pin_0
  N53: TOP_SHIFT_REGISTER.GPA0, LEDS_TOP.pin1
  N54: TOP_SHIFT_REGISTER.GPA1, LEDS_TOP.pin2
  N55: TOP_SHIFT_REGISTER.GPA2, LEDS_TOP.pin3
  N56: TOP_SHIFT_REGISTER.GPA3, LEDS_TOP.pin4
  N57: TOP_SHIFT_REGISTER.GPA4, LEDS_TOP.pin5
  N58: TOP_SHIFT_REGISTER.GPA5, LEDS_TOP.pin6
  N59: TOP_SHIFT_REGISTER.GPA6, LEDS_TOP.pin7
  N60: TOP_SHIFT_REGISTER.GPA7, LEDS_TOP.pin8

notes:
  SDA
  SCL
  GND
  5V
  3V3
  50
  51
  52
  53

custom parts:
  MCP23017 I2C I/O Expander: MCP23017 I2C 16-Channel I/O Expander
